# Fritzing sketch sketch (saved by Fritzing 0.9.2b)

parts:
  Part1 = Breakout Board for Electret Microphone
  Part2 = Arduino Uno (Rev3) - ICSP  # not connected
  Part3 = Arduino MP3 Player Shield
  SP1 = SPEAKER [package=pcb_mount_speaker]

nets:
  N1: Part1.VCC, Part3.3.3
  GND: Part1.GND, Part3.GND
  N2: Part1.AUD, Part3.A0
  N3: Part3.GBUF, SP1.+
  N4: Part3.RIGHT, SP1.-
